# Fritzing sketch CBA_2020_09_24 (saved by Fritzing 0.9.4)
circuit board: 10cm x 10cm
breadboards: 1

parts:
  J1 = STM32F103C8T6 blue mini board
  J3 = female pin header, 2 pins [form="♀ (female)"]  # not connected
  R12 = Resistor [tolerance=±5% resistance=220 package="0603 [SMD]"]
  R13 = Resistor [tolerance=±5% resistance=220 package="0603 [SMD]"]
  R14 = Resistor [tolerance=±5% resistance=220 package="0603 [SMD]"]
  R15 = Resistor [tolerance=±5% resistance=220 package="0603 [SMD]"]
  R16 = Resistor [tolerance=±5% resistance=220 package="0603 [SMD]"]
  R17 = Resistor [tolerance=±5% resistance=220 package="0603 [SMD]"]
  R18 = Resistor [tolerance=±5% resistance=220 package="0603 [SMD]"]
  R19 = Resistor [tolerance=±5% resistance=220 package="0603 [SMD]"]
  R20 = Resistor [tolerance=±5% resistance=220 package="0603 [SMD]"]  # not connected
  R21 = Resistor [tolerance=±5% resistance=220 package="0603 [SMD]"]  # not connected
  B5 = male pin header, 3 pins [form="♂ (male)"]
  B6 = male pin header, 2 pins [form="♂ (male)"]  # not connected
  B7 = male pin header, 2 pins [form="♂ (male)"]  # not connected
  B4 = male pin header, 2 pins [form="♂ (male)"]
  B2 = male pin header, 6 pins [form="♂ (male)"]
  BME280 = BME280r2 [package=lga8]  # not connected
  PCF8574 = PCF8574 [package="DIP16 [THT]"]
  Joystick = Thumb Joystick [package=joystick]
  U5 = MCP73831 [package=sot23-5]
  JP1 = Header 2 [package=jst-2-pth-kit]
  R22 = Resistor [tolerance=±5% resistance=10k package="0603 [SMD]"]
  PC13 = smd LED [color="Green (560nm)" package="0603 [SMD]"]  # not connected
  PWR1 = smd LED [color="Red (633nm)" package="0603 [SMD]"]  # not connected
  D2 = DIODE-SCHOTTKY [package=sma-diode]
  74VHC125MTC = TSSOP14 [chip_label=IC package=TSSOP]  # not connected
  OLED = 27 pin OLED  # not connected
  LM75 = MSOP8 [chip_label=IC package=MSOP8]  # not connected
  Buzzer = Buzzer 12mm [package=buzzer-cmt1102]  # not connected
  Flash = SPI_FLASH-X25XX [package=so08]  # not connected
  7_SegmentG1 = 7 Segment DisplayG
  SDA = male pin header, 3 pins [form="♂ (male)"]
  SCL = male pin header, 3 pins [form="♂ (male)"]
  U8 = microSD Socket [package=micro-sd-socket-pp]  # not connected

nets (from the schematic view):
  N1: J1.A9, B2.pin2
  N2: J1.A10, B2.pin3
  N3: J1.B6, SCL.pin1
  N4: J1.B7, SDA.pin1
  N5: J1.B8, SCL.pin3
  N6: J1.B9, SDA.pin3
  N7: J1.G, J1.GND, B4.pin1, B2.pin6
  3.3V: J1.3.3V, PCF8574.VCC
  N8: J1.C14, PCF8574.INT
  N9: R12.Pin_0, 7_SegmentG1.Segment_A
  N10: R12.Pin_1, PCF8574.P0
  N11: R13.Pin_0, 7_SegmentG1.Segment_B
  N12: R13.Pin_1, PCF8574.P1
  N13: R14.Pin_0, 7_SegmentG1.Segment_C
  N14: R14.Pin_1, PCF8574.P2
  N15: R15.Pin_0, PCF8574.P3
  N16: R15.Pin_1, 7_SegmentG1.Segment_D
  N17: R16.Pin_0, PCF8574.P4
  N18: R16.Pin_1, 7_SegmentG1.Segment_E
  N19: R17.Pin_0, PCF8574.P5
  N20: R17.Pin_1, 7_SegmentG1.Segment_F
  N21: R18.Pin_0, PCF8574.P6
  N22: R18.Pin_1, 7_SegmentG1.Segment_G
  N23: R19.Pin_0, 7_SegmentG1.Segment_DP
  N24: B5.pin2, U5.VIN, D2.C
  N25: B5.pin3, U5.VSS, JP1.1, R22.Pin_0
  N26: B4.pin2, PCF8574.GND, 7_SegmentG1.common_cathode#3
  N27: PCF8574.P7, Joystick.SEL+
  N28: PCF8574.SCL, SCL.pin2
  N29: PCF8574.SDA, SDA.pin2
  N30: Joystick.SEL-, 7_SegmentG1.common_cathode#8
  N31: U5.VBAT, JP1.2, D2.A
  N32: U5.PROG, R22.Pin_1

notes:
  PA0
  G
  G G3.3
  VBAT
  3.3
  RX
  TX
  5V G
  CBA_2020_09_24

custom parts:
  7 Segment DisplayG: 7 Segment Display with common cathode.(fixed G)
