# Fritzing sketch CBA_2020_10_01 (saved by Fritzing 0.9.4)
circuit board: 10cm x 10cm
breadboards: 1

parts:
  J1 = STM32F103C8T6 blue mini board
  J11 = female pin header, 2 pins [form="♀ (female)"]
  R12 = Resistor [tolerance=±5% resistance=220 package="0603 [SMD]"]
  R13 = Resistor [tolerance=±5% resistance=220 package="0603 [SMD]"]
  R14 = Resistor [tolerance=±5% resistance=220 package="0603 [SMD]"]
  R15 = Resistor [tolerance=±5% resistance=220 package="0603 [SMD]"]
  R16 = Resistor [tolerance=±5% resistance=220 package="0603 [SMD]"]
  R17 = Resistor [tolerance=±5% resistance=220 package="0603 [SMD]"]
  R18 = Resistor [tolerance=±5% resistance=220 package="0603 [SMD]"]
  R19 = Resistor [tolerance=±5% resistance=220 package="0603 [SMD]"]
  R20 = Resistor [tolerance=±5% resistance=220 package="0603 [SMD]"]
  R21 = Resistor [tolerance=±5% resistance=220 package="0603 [SMD]"]
  J5 = male pin header, 3 pins [form="♂ (male)"]
  J6 = male pin header, 2 pins [form="♂ (male)"]
  J7 = male pin header, 2 pins [form="♂ (male)"]
  J4 = male pin header, 2 pins [form="♂ (male)"]
  J10 = male pin header, 6 pins [form="♂ (male)"]
  BME280 = BME280r2 [package=lga8]  # not connected
  PCF8574 = PCF8574 [package="DIP16 [THT]"]
  Joystick = Thumb Joystick [package=joystick]
  U5 = MCP73831 [package=sot23-5]
  JP1 = Header 2 [package=jst-2-pth-kit]
  R22 = Resistor [tolerance=±5% resistance=10k package="0603 [SMD]"]
  PC13 = smd LED [color="Green (560nm)" package="0603 [SMD]"]  # not connected
  PWR1 = smd LED [color="Red (633nm)" package="0603 [SMD]"]  # not connected
  D2 = DIODE-SCHOTTKY [package=sma-diode]
  74VHC125MTC = TSSOP14 [chip_label=IC package=TSSOP]  # not connected
  OLED = 27 pin OLED  # not connected
  LM75 = MSOP8 [chip_label=IC package=MSOP8]  # not connected
  Buzzer = Buzzer 12mm [package=buzzer-cmt1102]  # not connected
  Flash = SPI_FLASH-X25XX [package=so08]  # not connected
  7_SegmentG1 = 7 Segment DisplayG
  SDA = male pin header, 3 pins [form="♂ (male)"]
  SCL = male pin header, 3 pins [form="♂ (male)"]
  U8 = microSD Socket [package=micro-sd-socket-pp]  # not connected
  J8 = male pin header, 7 pins [form="♂ (male)"]  # not connected
  J9 = male pin header, 7 pins [form="♂ (male)"]  # not connected
  J3 = STM32F103C8T6 blue mini board
  SDAslave = male pin header, 3 pins [form="♂ (male)"]
  SCLslave = male pin header, 3 pins [form="♂ (male)"]

nets:
  N1: J1.A8, J5.pin1
  N2: J1.A9, J10.pin2
  N3: J1.A10, J10.pin3
  N4: J1.B6, SCL.pin1, SCLslave.pin1
  N5: J1.B7, SDA.pin1, SDAslave.pin1
  N6: J1.B8, SCL.pin3
  N7: J1.B9, SDA.pin3
  5V: J1.5V, J5.pin2, U5.VIN, D2.C
  GND: J1.G, J1.GND, J5.pin3, J10.pin6, PCF8574.GND, Joystick.SEL-, Joystick.H-, Joystick.V-, U5.VSS, JP1.1, R22.Pin_0, 7_SegmentG1.common_cathode, J3.G, J3.GND
  N8: J1.3.3V, J11.pin2, J4.pin1
  N9: J1.C14, PCF8574.INT
  N10: J1.A0, Joystick.H
  N11: J1.A2, Joystick.V
  N12: J1.A3, R19.Pin_1
  N13: J1.B0, J7.pin1
  N14: J1.B1, J6.pin1
  N15: R12.Pin_0, 7_SegmentG1.Segment_A
  N16: R12.Pin_1, PCF8574.P0
  N17: R13.Pin_0, 7_SegmentG1.Segment_B
  N18: R13.Pin_1, PCF8574.P1
  N19: R14.Pin_0, 7_SegmentG1.Segment_C
  N20: R14.Pin_1, PCF8574.P2
  N21: R15.Pin_0, PCF8574.P3
  N22: R15.Pin_1, 7_SegmentG1.Segment_D
  N23: R16.Pin_0, PCF8574.P4
  N24: R16.Pin_1, 7_SegmentG1.Segment_E
  N25: R17.Pin_0, PCF8574.P5
  N26: R17.Pin_1, 7_SegmentG1.Segment_F
  N27: R18.Pin_0, PCF8574.P6
  N28: R18.Pin_1, 7_SegmentG1.Segment_G
  N29: R19.Pin_0, 7_SegmentG1.Segment_DP
  N30: R20.Pin_1, R21.Pin_1
  N31: J4.pin2, PCF8574.VCC, Joystick.V+, Joystick.H+
  N32: PCF8574.P7, Joystick.SEL+
  N33: PCF8574.SCL, SCL.pin2
  N34: PCF8574.SDA, SDA.pin2
  N35: U5.VBAT, JP1.2, D2.A
  N36: U5.PROG, R22.Pin_1
  N37: J3.B6, SCLslave.pin2
  N38: J3.B7, SDAslave.pin2

notes:
  PA0
  G
  G G3.3
  VBAT
  3.3
  RX
  TX
  5V G
  CBA_2020_10_01
  J0

custom parts:
  7 Segment DisplayG: 7 Segment Display with common cathode.(fixed G)
